# Fritzing sketch brick_display (saved by Fritzing 0.9.10b)

parts:
  Mod1 = Raspberry Pi 4B
  Part3 = Adafruit 2.7in 400x240 SHARP Memory Display

nets:
  N1: Mod1.GPIO23, Part3.SCS_5V
  3V3: Mod1.3V3, Part3.3.3V
  N2: Mod1.GPIO24, Part3.DISP_5V
  N3: Mod1.GPIO10, Part3.SI_5V
  GND: Mod1.GND, Part3.GND
  N4: Mod1.GPIO25, Part3.EXTCOMIN_5V
  N5: Mod1.GPIO11, Part3.SCLK_5V
