# Fritzing sketch brick_power (saved by Fritzing 0.9.10b)
breadboards: 1

parts:
  Mod1 = Raspberry Pi 4B
  Part2 = Adafruit BQ24074 Solar-DC-USB Lipo Charger
  Part1 = Lithium Ion Battery Pack 3.7V 6600mAh [part_number=353]
  LED1 = LED - 5mm [color="Green (555nm)" current=0.030 package="5 mm [THT]"]
  LED2 = LED - 5mm [color="Red (633nm)" current=0.030 package="5 mm [THT]"]
  S1 = Toggle Switch [package=THT]
  S2 = Taiway 100-SP-X-T1 SPDT Miniature Toggle Switch [part_number=100-SP-X-T1-0-0-B1-M2 package=THT]
  R1 = Resistor [tolerance=±5% power=0.25 resistance=10000 package=THT]

nets:
  N1: Mod1.5V, S2.COM
  GND: Mod1.GND, Part2.GND, Part1.negative
  N2: Part2.VLIPO, Part1.positive
  N3: Part2.OUT, LED1.anode, S1.L2, S2.L1, R1.Pin_0
  N4: Part2.!CHG, LED2.cathode
  N5: Part2.!PGOOD, LED1.cathode
  N6: Part2.!CE, S1.COM
  N7: LED2.anode, R1.Pin_1

custom parts:
  Lithium Ion Battery Pack 3.7V 6600mAh: This lithium ion pack is made of 3 balanced 2200mAh cells for a total of 6600mA capacity! The cells are connected in parallel and spot-welded to a protection circuit that provides over-voltage, under-voltage and over-current protection. Each cell can provide 0.5C of current (1.1 A per) so all together the peak current you can draw is over 3.3 Amps. Note that these batteries are not designed to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
